# Fritzing sketch Schaltplan_Freezer_Control (saved by Fritzing 0.9.6b)
circuit board: 8.46667cm x 5.64444cm
breadboards: 1

parts:
  Bauteil1 = Arduino Uno (Rev3) - ICSP
  DS1 = DS18B20 1-Wire Temperature Sensor [part_number=DS18B20]
  DS2 = DS18B20 1-Wire Temperature Sensor [part_number=DS18B20]
  DS3 = DS18B20 1-Wire Temperature Sensor [part_number=DS18B20]
  J1 = Piezo Speaker
  R1 = Resistor [tolerance=±5% resistance=1M package="0603 [SMD]"]
  IC1 = Voltage Regulator [package=to220-igo]
  C1 = Electrolytic Capacitor [capacitance=1µF voltage=35V package="100 mil [THT, electrolytic]"]
  C2 = Electrolytic Capacitor [capacitance=1µF voltage=35V package="100 mil [THT, electrolytic]"]
  C3 = Electrolytic Capacitor [capacitance=1µF voltage=35V package="100 mil [THT, electrolytic]"]
  C4 = Electrolytic Capacitor [capacitance=1µF voltage=35V package="100 mil [THT, electrolytic]"]
  IC2 = Voltage Regulator [package=to220-adj]
  J4 = Screw terminal - 2 pins [package=THT]
  J5 = Screw terminal - 2 pins [package=THT]
  Bauteil2 = Adafruit 1.54" Tri-Color eInk / ePaper Display with SRAM [part_number=3625]
  KY-1 = Keyes Relay [package=THT]
  KY-2 = Keyes Relay [package=THT]
  S1 = SPST Switch [package=switche-dpdt]
  J9 = Screw terminal - 2 pins [package=THT]
  J10 = Screw terminal - 2 pins [package=THT]
  S2 = SPST Switch [package=switche-dpdt]
  J7 = Screw terminal - 2 pins [package=THT]
  D2 = Rectifier Diode [package="Melf DO-213 AA [SMD]"]
  D3 = Rectifier Diode [package="Melf DO-213 AA [SMD]"]
  R2 = Resistor [tolerance=±5% power=0.25 resistance=1.5k package=THT]
  C5 = Ceramic Capacitor [capacitance=100nF voltage=35V package="100 mil [THT, multilayer]"]

nets:
  N1: Bauteil1.A2, R1.Pin_0, IC1.OUT, C1.+
  N2: Bauteil1.D8, Bauteil2.RESET
  N3: Bauteil1.D9_PWM, Bauteil2.DC
  N4: Bauteil1.D10_PWM/SS, Bauteil2.DISPCS
  N5: Bauteil1.D11_PWM/MOSI, Bauteil2.MISO
  N6: Bauteil1.D13/SCK, Bauteil2.SCLK
  GND: Bauteil1.GND, DS1.GND, DS2.GND, DS3.GND, J1.pin1, R1.Pin_1, C1.-, C2.-, C3.-, C4.-, IC2.ADJ, J4.pin1, Bauteil2.GND, KY-1.ground, KY-2.ground, C5.1
  N7: Bauteil1.D2, KY-2.power
  N8: Bauteil1.D3_PWM, KY-1.power
  N9: Bauteil1.D4, J1.pin2
  N10: Bauteil1.D5_PWM, DS1.DQ, DS2.DQ, DS3.DQ, R2.Pin_0
  N11: Bauteil1.D7, Bauteil2.BUSY
  3V3: Bauteil1.3V3, Bauteil2.3.3V
  VDD: Bauteil1.5V, DS1.VDD, DS2.VDD, DS3.VDD, KY-1.sSgnal, KY-2.sSgnal, J7.pin2, R2.Pin_1, C5.0
  N12: Bauteil1.VIN, C4.+, IC2.OUT
  N13: IC1.GND, C2.+, J5.pin1, KY-1.C
  N14: C3.+, IC2.IN, J4.pin2, S2.O
  N15: KY-1.NO, J9.pin1, D3.anode
  N16: KY-2.C, S1.O, S1.P
  N17: KY-2.NO, D2.anode
  N18: S1.S, S2.S, J7.pin1
  N19: J10.pin1, D2.cathode, D3.cathode

notes:
  Freezer Relay
  Solar Power Indicator Relay
  Output Solar Power Indicator 12V
  12V Battery Power
  Switch freezer via car relay 12V / 30A
  Power Switch 12V
  Freezer Control Switch

custom parts:
  Adafruit 1.54" Tri-Color eInk / ePaper Display with SRAM: This small 1.54" tri-color display has 152x152 black and red ink pixels and a white-ish background. Using our Arduino library, you can create a 'frame buffer' with what pixels you want to have activated and then write that out to the display. We tossed a small SRAM chip on the back. This chip shares the SPI port the eInk display uses, so you only need one extra pin. And, no more frame-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
  Keyes Relay: The Keyes 5V relay module is suitable for SCM development, home appliance control. It uses a 5V~12V TIL control signal which can control DC / AC signal.
